// Logisim project exp_2_1.circ as structural Verilog: 1 circuit, main circuit main
module main (
  input  x,
  input  y,
  input  z,
  output f
);

  wire nx, nxy, t1, t2, xy;

  not not_1 (nx, x);
  and and_1 (xy, x, y);
  not not_2 (nxy, xy);
  and and_2 (t1, nx, y, z);
  and and_3 (t2, nxy, z);
  or or_1 (f, t1, t2, xy);
endmodule
