// Logisim project exp_2_2.circ as structural Verilog: 1 circuit, main circuit main
module main (
  input  X,
  input  Y,
  input  Z,
  output F
);

  wire a1, a2, a3, nX, nY, nZ;

  not not_1 (nX, X);
  not not_2 (nY, Y);
  not not_3 (nZ, Z);
  and and_1 (a1, Y, Z);
  and and_2 (a2, nX, nY);
  and and_3 (a3, nY, nZ);
  or or_1 (F, a1, a2, a3);
endmodule
