// Logisim project exp_2_3.circ as structural Verilog: 1 circuit, main circuit main
module main (
  input  x,
  input  y,
  input  z,
  output F
);

  wire A, B, Fs, ny, yz;

  not not_1 (ny, y);
  and and_1 (yz, y, z);
  nor nor_1 (A, x, yz);
  nand nand_1 (B, ny, x);
  nor nor_2 (F, A, B);
  and and_2 (Fs, x, ny);
  // Probe on Fs
endmodule
