// Logisim project mux_74ls151.circ as structural Verilog: 1 circuit, main circuit main
module main (
  input  x,
  input  y,
  input  z,
  output f
);

  wire fbar, m0, m1, m2, m3, m4, m5, m6, m7, nx, ny, nz;

  not not_1 (nx, x);
  not not_2 (ny, y);
  not not_3 (nz, z);
  and and_1 (m0, nx, ny, nz);
  and and_2 (m1, nx, ny, z);
  and and_3 (m2, nx, y, nz);
  and and_4 (m3, nx, y, z);
  and and_5 (m4, x, ny, nz);
  and and_6 (m5, x, ny, z);
  and and_7 (m6, x, y, nz);
  and and_8 (m7, x, y, z);
  or or_1 (f, m1, m2, m4, m7);
  not not_4 (fbar, f);
  // Probe on fbar
endmodule
