// Logisim project dec_74ls138.circ as structural Verilog: 1 circuit, main circuit main
module main (
  input  x,
  input  y,
  input  z,
  output f
);

  wire nY0, nY1, nY2, nY3, nY4, nY5, nY6, nY7, t1, t2, U1_pin4, U1_pin5, U1_pin6, U1_pin8, U1_pin16, U2_pin7,
       U2_pin14, U3_pin7, U3_pin14;

  // Probe on nothing
  _74138 #(.VccGndPorts("true")) U1 (
    .pin1(z), .pin2(y), .pin3(x), .pin4(U1_pin4), .pin5(U1_pin5), .pin6(U1_pin6), .pin7(nY7), .pin8(U1_pin8),
    .pin16(U1_pin16), .pin15(nY0), .pin14(nY1), .pin13(nY2), .pin12(nY3), .pin11(nY4), .pin10(nY5), .pin9(nY6));
  // Probe on nothing
  // Probe on nothing
  // Probe on nothing
  // Probe on nothing
  // Probe on nothing
  // Probe on nothing
  // Probe on nothing
  _7408 #(.VccGndPorts("true")) U2 (
    .pin1(nY0), .pin2(nY2), .pin3(t1), .pin4(nY5), .pin5(nY7), .pin6(t2), .pin7(U2_pin7), .pin14(U2_pin14));  // open: pin13, pin12, pin11, pin10, pin9, pin8
  _7400 #(.VccGndPorts("true")) U3 (
    .pin1(t1), .pin2(t2), .pin3(f), .pin7(U3_pin7), .pin14(U3_pin14));  // open: pin4, pin5, pin6, pin13, pin12, pin11, pin10, pin9, pin8
  // also tied to GND on the sheet: {U1_pin4, U1_pin5, U1_pin8, U2_pin7, U3_pin7}
  // also tied to VCC on the sheet: {U1_pin16, U1_pin6, U2_pin14, U3_pin14}
endmodule
