// Logisim project full_adder.circ as structural Verilog: 1 circuit, main circuit main
module main (
  input  A,
  input  B,
  input  Ci,
  output S,
  output Co
);

  wire C1, C2, T1;

  xor xor_1 (T1, A, B);
  and and_1 (C1, A, B);
  xor xor_2 (S, T1, Ci);
  and and_2 (C2, T1, Ci);
  or or_1 (Co, C1, C2);
endmodule
