// Logisim project dff74ls74.circ as structural Verilog: 1 circuit, main circuit main
module main (
  input  D,
  input  CLK,
  input  PRE,
  input  CLR,
  output Q,
  output QN
);

  wire U1_pin7, U1_pin14;

  _7474 #(.VccGndPorts("true")) U1 (
    .pin1(CLR), .pin2(D), .pin3(CLK), .pin4(PRE), .pin5(Q), .pin6(QN), .pin7(U1_pin7), .pin14(U1_pin14));  // open: pin13, pin12, pin11, pin10, pin9, pin8
  // also tied to GND on the sheet: U1_pin7
  // also tied to VCC on the sheet: U1_pin14
endmodule
