// Logisim project fsm_fig34.circ as structural Verilog: 1 circuit, main circuit main
module main (
  input  clk,
  input  clr,
  input  X,
  output S1,
  output S0
);

  wire nS0, nS1, S0p, S1p, SUM, U1_pin4, U1_pin7, U1_pin10, U1_pin14, U2_pin7, U2_pin14, U3_pin7, U3_pin14,
       U4_pin7, U4_pin14;

  _7474 #(.VccGndPorts("true")) U1 (
    .pin1(clr), .pin2(S1p), .pin3(clk), .pin4(U1_pin4), .pin5(S1), .pin6(nS1), .pin7(U1_pin7),
    .pin14(U1_pin14), .pin13(clr), .pin12(S0p), .pin11(clk), .pin10(U1_pin10), .pin9(S0), .pin8(nS0));
  _7408 #(.VccGndPorts("true")) U2 (
    .pin1(X), .pin2(S0), .pin3(S1p), .pin7(U2_pin7), .pin14(U2_pin14));  // open: pin4, pin5, pin6, pin13, pin12, pin11, pin10, pin9, pin8
  _7408 #(.VccGndPorts("true")) U3 (
    .pin1(X), .pin2(SUM), .pin3(S0p), .pin7(U3_pin7), .pin14(U3_pin14));  // open: pin4, pin5, pin6, pin13, pin12, pin11, pin10, pin9, pin8
  _7432 #(.VccGndPorts("true")) U4 (
    .pin1(nS1), .pin2(nS0), .pin3(SUM), .pin7(U4_pin7), .pin14(U4_pin14));  // open: pin4, pin5, pin6, pin13, pin12, pin11, pin10, pin9, pin8
  // also tied to GND on the sheet: {U1_pin7, U2_pin7, U3_pin7, U4_pin7}
  // also tied to VCC on the sheet: {U1_pin14, U1_pin4, U1_pin10, U2_pin14, U3_pin14, U4_pin14}
endmodule
