// Logisim project adder4.circ as structural Verilog: 1 circuit, main circuit main
module main (
  input  A0,
  input  A1,
  input  A2,
  input  A3,
  input  B0,
  input  B1,
  input  B2,
  input  B3,
  input  Ci,
  output S3,
  output S2,
  output S1,
  output S0,
  output C4
);

  wire C1, C2, C3, S0_t, S0_x, S0_y, S1_t, S1_x, S1_y, S2_t, S2_x, S2_y, S3_t, S3_x, S3_y;

  xor xor_1 (S0_t, A0, B0);
  and and_1 (S0_x, A0, B0);
  xor xor_2 (S0, S0_t, Ci);
  and and_2 (S0_y, S0_t, Ci);
  or or_1 (C1, S0_x, S0_y);
  xor xor_3 (S1_t, A1, B1);
  and and_3 (S1_x, A1, B1);
  xor xor_4 (S1, S1_t, C1);
  and and_4 (S1_y, S1_t, C1);
  or or_2 (C2, S1_x, S1_y);
  xor xor_5 (S2_t, A2, B2);
  and and_5 (S2_x, A2, B2);
  xor xor_6 (S2, S2_t, C2);
  and and_6 (S2_y, S2_t, C2);
  or or_3 (C3, S2_x, S2_y);
  xor xor_7 (S3_t, A3, B3);
  and and_7 (S3_x, A3, B3);
  xor xor_8 (S3, S3_t, C3);
  and and_8 (S3_y, S3_t, C3);
  or or_4 (C4, S3_x, S3_y);
endmodule
