// Logisim project counter_0_7.circ as structural Verilog: 1 circuit, main circuit main
module main (
  input  clk,
  input  clr,
  output Q2,
  output Q1,
  output Q0
);

  wire nQ0, nQ1, nQ2, U1_pin4, U1_pin7, U1_pin14, U2_pin4, U2_pin7, U2_pin10, U2_pin14;

  _7474 #(.VccGndPorts("true")) U1 (
    .pin1(clr), .pin2(nQ0), .pin3(clk), .pin4(U1_pin4), .pin5(Q0), .pin6(nQ0), .pin7(U1_pin7),
    .pin14(U1_pin14));  // open: pin13, pin12, pin11, pin10, pin9, pin8
  _7474 #(.VccGndPorts("true")) U2 (
    .pin1(clr), .pin2(nQ1), .pin3(nQ0), .pin4(U2_pin4), .pin5(Q1), .pin6(nQ1), .pin7(U2_pin7),
    .pin14(U2_pin14), .pin13(clr), .pin12(nQ2), .pin11(nQ1), .pin10(U2_pin10), .pin9(Q2), .pin8(nQ2));
  // also tied to GND on the sheet: {U1_pin7, U2_pin7}
  // also tied to VCC on the sheet: {U1_pin14, U1_pin4, U2_pin14, U2_pin4, U2_pin10}
endmodule
